# Fritzing sketch Untitled Sketch (saved by Fritzing 0.9.2b)
breadboards: 1

parts:
  R1 = Resistor [tolerance=±5% resistance=150 package=THT]
  R2 = Resistor [tolerance=±5% resistance=150 package=THT]
  GREEN_LED = LED - 5mm [color="Green (570nm)" package="5 mm [THT]"]
  U1 = atmega328 [package=dip]
  XTAL1 = Crystal [frequency="16 Mhz" package=THT]
  RED_LED = LED - 5mm [color="Red (633nm)" package="5 mm [THT]"]
  Serial_UART = double row female pin header, 4 pins [form="♀ (female)"]

nets:
  GND: R1.Pin_0, R2.Pin_0, GREEN_LED.cathode, U1.GND, RED_LED.cathode, Serial_UART.pin3
  N1: R1.Pin_1, R2.Pin_1, GREEN_LED.anode, U1.D12
  N2: U1.D0_(RX), Serial_UART.pin1
  N3: U1.VCC, Serial_UART.pin2
  N4: U1.XLAT1, XTAL1.pin_1
  N5: U1.XLAT2, XTAL1.pin_0
  N6: U1.D11_(PWM), RED_LED.anode

notes:
  TX
  VCC 5V
  GND
  VCC
